# Fritzing sketch hardware_schematichs (saved by Fritzing 0.9.9b)

parts:
  Raspberry_Pi_1 = Raspberry Pi 3 [part_number=RPI-3-V1.2]
  Componente4 = 16-Channel 12-bit PWM Servo Driver - I2C [part_number=815]
  J1 = Basic Servo
  J2 = Basic Servo
  J3 = Basic Servo
  VCC2 = 4 x AAA Battery Mount
  CAMERA1 = TTL Serial JPEG Camera  # not connected

nets:
  3V3: Raspberry_Pi_1.3v3, Componente4.VCC
  N1: Raspberry_Pi_1.GPIO2, Componente4.SDA
  N2: Raspberry_Pi_1.GPIO3, Componente4.SCL
  GND: Raspberry_Pi_1.GND, Componente4.GND, J1.gnd, J2.gnd, J3.gnd, VCC2.-
  N3: Componente4.PWRIN, VCC2.+
  N4: Componente4.PWM2, J2.pulse
  VCC: Componente4.5.0V, J1.vcc, J2.vcc, J3.vcc
  N5: Componente4.PWM1, J3.pulse
  N6: Componente4.PWM0, J1.pulse

custom parts:
  16-Channel 12-bit PWM Servo Driver - I2C: You want to make a cool robot, maybe a hexapod walker, or maybe just a piece of art with a lot of moving parts. Or maybe you want to drive a lot of LEDs with precise PWM output. Using only two pins, control 16 free-running PWM outputs! You can even chain up 62 breakouts to control up to 992 PWM outputs.
  TTL Serial JPEG Camera: TTL Serial JPEG Camera with NTSC Out
